# Fritzing sketch Esqeuma (saved by Fritzing 0.9.2b)
breadboards: 2

parts:
  Parte1 = Arduino Micro (Rev3)  # not connected
  IC1 = L293D [package=THT]
  M1 = DC Motor

nets:
  N1: IC1.Out_1_(_Controlled_by_Enable_1_), M1.pin_2
  N2: IC1.Out_2_(_Controlled_by_Enable_1_), M1.pin_1
  N3: IC1.+Vmotor, IC1.+V
