# Fritzing sketch Acelerometro (saved by Fritzing 0.9.3b)
breadboards: 1

parts:
  Componente1 = Arduino Nano (Rev3.0) (ICSP)
  LED1 = LED - 3mm [color="Red (633nm)" package="3 mm [THT]"]
  LED2 = LED - 3mm [color="Yellow (595nm)" package="3 mm [THT]"]
  LED3 = LED - 3mm [color="Green (570nm)" package="3 mm [THT]"]
  R1 = Resistor [tolerance=±5% resistance=220 package="0603 [SMD]"]
  R3 = Resistor [tolerance=±5% resistance=220 package="0603 [SMD]"]
  R4 = Resistor [tolerance=±5% resistance=10k package="0603 [SMD]"]
  R2 = Resistor [tolerance=±5% resistance=220 package="0603 [SMD]"]
  U2 = MMA7361 [package=lga14]

nets:
  N1: Componente1.GND, R1.Pin_1, R3.Pin_0, R4.Pin_1, R2.Pin_1, U2.0GD, U2.GSELECT, U2.ST
  N2: Componente1.D2, LED2.anode
  N3: Componente1.D4, LED1.anode, LED3.anode
  5V: Componente1.5V, U2.5v
  N4: Componente1.A4, U2.ZOUT
  N5: Componente1.A3, U2.YOUT
  N6: Componente1.A0, U2.XOUT
  N7: LED1.cathode, R2.Pin_0
  N8: LED2.cathode, R1.Pin_0
  N9: LED3.cathode, R3.Pin_1
  N10: R4.Pin_0, U2.3v3

custom parts:
  MMA7361: 3-axis 1.5/6g analog output accelerometer
