# Fritzing sketch Esquema (saved by Fritzing 0.9.2b)

parts:
  Parte1 = Arduino Nano (Rev3.0)
  Parte2 = SRF05 Ultrasonic Rangefinder
  LCD2 = LCD screen
  LCM1602_IIC2 = LCM1602 IIC [part_number="LCM1602 IIC" chip_label="LCM1602 IIC" package="DIP (Dual Inline) [THT]"]

nets:
  GND: Parte1.GND, Parte2.GND, LCM1602_IIC2.GND
  N1: Parte1.D5, Parte2.Echo
  N2: Parte1.D6, Parte2.Trig
  N3: Parte1.A5, LCM1602_IIC2.SCL
  N4: Parte1.A4, LCM1602_IIC2.SDA
  VCC: Parte2.VCC, LCM1602_IIC2.VCC
  VSS: LCD2.VSS, LCM1602_IIC2.VSS
  VDD: LCD2.VDD, LCM1602_IIC2.VDD
  N5: LCD2.V0, LCM1602_IIC2.V0
  N6: LCD2.RS, LCM1602_IIC2.RS
  N7: LCD2.R/W, LCM1602_IIC2.RW
  N8: LCD2.E, LCM1602_IIC2.E
  N9: LCD2.DB0, LCM1602_IIC2.D0
  N10: LCD2.DB1, LCM1602_IIC2.D1
  N11: LCD2.DB2, LCM1602_IIC2.D2
  N12: LCD2.DB3, LCM1602_IIC2.D3
  N13: LCD2.DB4, LCM1602_IIC2.D4
  N14: LCD2.DB5, LCM1602_IIC2.D5
  N15: LCD2.DB6, LCM1602_IIC2.D6
  N16: LCD2.DB7, LCM1602_IIC2.D7
  N17: LCD2.LED+, LCM1602_IIC2.A
  N18: LCD2.LED-, LCM1602_IIC2.K
  N19: LCM1602_IIC2.LED_A, LCM1602_IIC2.LED_B

custom parts:
  LCM1602 IIC: I2C-Module to use a 1602 or 2004 LCD on with the wire.h libory Serial LCD Modul
